# Fritzing sketch schematic (saved by Fritzing 0.9.2b)
breadboards: 1

parts:
  VCC1 = Battery
  U1 = LM 358 Dual Op-Amp [package="DIP8 [THT]"]  # not connected
  LED1 = LED - 5mm [color="Red (633nm)" package="5 mm [THT]"]
  R1 = Rotary Potentiometer (Small) [maximum_resistance=100kΩ package=THT]
  R2 = Resistor [tolerance=±5% resistance=220 package=THT]

nets:
  N1: VCC1.-, R1.leg2, R2.Pin_0
  N2: VCC1.+, R1.leg1
  N3: LED1.cathode, R2.Pin_1
