# Fritzing sketch schematic (saved by Fritzing 0.9.2b)
breadboards: 1

parts:
  VCC1 = Battery
  LED1 = LED - 5mm [color="Red (635nm)" package="5 mm [THT]"]
  R2 = Resistor [tolerance=±5% resistance=220 package=THT]
  R3 = Resistor [tolerance=±5% resistance=220 package=THT]
  LED2 = LED - 5mm [color="Infrared (940nm)" package="5 mm [THT]"]

nets:
  N1: VCC1.-, LED1.cathode
  N2: VCC1.+, R2.Pin_1
  N3: LED1.anode, R2.Pin_0
  N4: R3.Pin_0, LED2.anode
