# Fritzing sketch schematic (saved by Fritzing 0.9.2b)
breadboards: 1

parts:
  Bauteil1 = Arduino Uno (Rev3)
  R1 = Resistor [tolerance=±5% resistance=1k package=THT]
  LED1 = LED - 5mm [color="Red (633nm)" package="5 mm [THT]"]
  S1 = Pushbutton [package="[THT]"]

nets:
  N1: Bauteil1.D10_PWM/SS, S1.Pin_1, S1.Pin_2
  N2: Bauteil1.D11_PWM/MOSI, LED1.anode
  N3: Bauteil1.GND, R1.Pin_0, S1.Pin_3, S1.Pin_4
  N4: R1.Pin_1, LED1.cathode
