# Fritzing sketch schematic (saved by Fritzing 0.9.2b)
breadboards: 1

parts:
  R2 = Rotary Potentiometer (Small) [maximum_resistance=100kΩ package=THT]
  Bauteil1 = Arduino Uno (Rev3)

nets:
  N1: R2.leg1, Bauteil1.GND
  N2: R2.wiper, Bauteil1.A0
  N3: R2.leg2, Bauteil1.5V
