# Fritzing sketch schematic (saved by Fritzing 0.9.2b)
breadboards: 1

parts:
  7_Segment1 = 7 Segment Display
  R1 = Resistor [tolerance=±5% resistance=1k package=THT]
  R2 = Resistor [tolerance=±5% resistance=1k package=THT]
  R3 = Resistor [tolerance=±5% resistance=1k package=THT]
  R4 = Resistor [tolerance=±5% resistance=1k package=THT]
  R5 = Resistor [tolerance=±5% resistance=1k package=THT]
  R6 = Resistor [tolerance=±5% resistance=1k package=THT]
  R7 = Resistor [tolerance=±5% resistance=1k package=THT]
  R8 = Resistor [tolerance=±5% resistance=1k package=THT]
  Bauteil1 = Arduino Uno (Rev3)
  7_Segment2 = 7 Segment Display  # not connected

nets:
  N1: 7_Segment1.Segment_A#1, R1.Pin_1
  N2: 7_Segment1.Segment_F, R2.Pin_1
  N3: 7_Segment1.Segment_E, R3.Pin_0
  N4: 7_Segment1.Segment_D, R4.Pin_0
  N5: 7_Segment1.Segment_DP, R6.Pin_0
  N6: 7_Segment1.Segment_C, R5.Pin_0
  N7: 7_Segment1.common_cathode#8, Bauteil1.A2, Bauteil1.A3, Bauteil1.A4/SDA, Bauteil1.A5/SCL, Bauteil1.GND
  N8: 7_Segment1.Segment_B, R8.Pin_1
  N9: 7_Segment1.Segment_A#10, R7.Pin_1
  N10: R1.Pin_0, Bauteil1.D8
  N11: R2.Pin_0, Bauteil1.D7
  N12: R3.Pin_1, Bauteil1.D6_PWM
  N13: R4.Pin_1, Bauteil1.D5_PWM
  N14: R5.Pin_1, Bauteil1.D4
  N15: R6.Pin_1, Bauteil1.D9_PWM
  N16: R7.Pin_0, Bauteil1.D2
  N17: R8.Pin_0, Bauteil1.D3_PWM

notes:
  2
  3
  4
  9
  8
  7
  5
  6
  GND
