# Fritzing sketch schematic (saved by Fritzing 0.9.3b)
breadboards: 2

parts:
  R2 = Resistor [tolerance=±5% resistance=1k package=THT]
  LED1 = LED - 5mm [color="Green (555nm)" package="5 mm [THT]"]
  Bauteil1 = Arduino Uno (Rev3)
  Bauteil2 = Arduino Uno (Rev3)
  LED2 = LED - 5mm [color="Yellow (585nm)" package="5 mm [THT]"]
  LED3 = LED - 5mm [color="Red (633nm)" package="5 mm [THT]"]
  R3 = Resistor [tolerance=±5% resistance=1k package=THT]
  R4 = Resistor [tolerance=±5% resistance=1k package=THT]
  R1 = Rotary Potentiometer (Small) [maximum_resistance=100kΩ package=THT]  # not connected

nets:
  N1: R2.Pin_0, LED1.anode
  N2: R2.Pin_1, Bauteil2.D9_PWM
  GND: LED1.cathode, Bauteil1.GND, Bauteil2.GND, LED2.cathode, LED3.cathode
  N3: Bauteil1.D2, Bauteil2.D3_PWM
  N4: Bauteil1.D3_PWM, Bauteil2.D2
  N5: Bauteil2.D10_PWM/SS, R3.Pin_1
  N6: Bauteil2.D11_PWM/MOSI, R4.Pin_1
  N7: LED2.anode, R3.Pin_0
  N8: LED3.anode, R4.Pin_0
